# Fritzing sketch touchswitch_v2.1_order (saved by Fritzing 0.9.4)
circuit board: 4.6cm x 3.8cm
breadboards: 1

parts:
  J1 = female pin header, 6 pins [form="♀ (female)"]
  Q1 = TRANSISTOR_NPN [package=to-92]
  R1 = Resistor [tolerance=±5% resistance=1k package=THT]
  PIC18(L)F1 = PIC16(L)F1824 [chip_label=PIC16(L)F1824 package="DIP (Dual Inline) [THT]"]
  J2 = female pin header, 6 pins [form="♀ (female)"]
  WeMos_D1_Mini2 = WeMos D1 Mini

nets:
  N1: J1.pin1, Q1.C
  N2: J1.pin2, WeMos_D1_Mini2.14
  N3: J1.pin3, WeMos_D1_Mini2.2
  N4: J1.pin4, PIC18(L)F1.RC4
  N5: J1.pin5, WeMos_D1_Mini2.0
  N6: J1.pin6, PIC18(L)F1.RC5
  N7: Q1.E, PIC18(L)F1.GND, WeMos_D1_Mini2.G
  N8: Q1.B, R1.Pin_0
  N9: R1.Pin_1, PIC18(L)F1.RC3
  VDD: PIC18(L)F1.VDD, J2.pin1, WeMos_D1_Mini2.3V3
  N10: PIC18(L)F1.RC1, WeMos_D1_Mini2.5
  N11: PIC18(L)F1.RC0, WeMos_D1_Mini2.RST
  N12: J2.pin2, WeMos_D1_Mini2.13
  N13: J2.pin3, WeMos_D1_Mini2.4
  N14: J2.pin4, WeMos_D1_Mini2.12
  N15: J2.pin5, WeMos_D1_Mini2.15

notes:
  *
  GND
  3V
  5V-IN
  E
  3V-OUT
  VDD

custom parts:
  PIC16(L)F1824: A DIP stand-in part for whatever IC you want. With 14 pins on a 300mil dual inline package (DIP) footprint.
  WeMos D1 Mini: The D1 mini is a mini wifi board based on ESP-8266EX.
